# Fritzing sketch Schematic (saved by Fritzing 0.9.4)
breadboards: 4

parts:
  Part1 = Arduino Mega 2560 (Rev3)
  R1 = Resistor [tolerance=±5% resistance=220 package=THT]
  R2 = Resistor [tolerance=±5% resistance=220 package=THT]
  R3 = Resistor [tolerance=±5% resistance=220 package=THT]
  S2 = Toggle Switch [package=THT]
  S3 = Toggle Switch [package=THT]
  S4 = Toggle Switch [package=THT]
  J1 = Basic Servo
  J2 = Basic Servo
  J3 = Basic Servo
  J4 = Basic Servo
  M1 = Stepper Motor - Bipolar  # not connected
  M2 = Stepper Motor - Bipolar  # not connected
  M3 = Stepper Motor - Bipolar  # not connected
  U2 = RELAY [package=relay-jzc]

nets:
  N1: Part1.D21/SCL, U2.COIL1
  GND: Part1.GND, S2.L1, S3.L1, S4.L1, J1.gnd, J2.gnd, J3.gnd, J4.gnd, U2.COIL2
  N2: Part1.D4_PWM, J4.pulse
  N3: Part1.D5_PWM, J3.pulse
  N4: Part1.D6_PWM, J2.pulse
  N5: Part1.D7_PWM, J1.pulse
  N6: Part1.5V, R1.Pin_0, R2.Pin_0, R3.Pin_0, U2.NO
  N7: Part1.D22, R1.Pin_1, S4.COM
  N8: Part1.D24, R2.Pin_1, S2.COM
  N9: Part1.D26, R3.Pin_1, S3.COM
  VCC: J1.vcc, J2.vcc, J3.vcc, J4.vcc, U2.MAIN

notes:
  TB6600 Stepper Motor Drivers
  Relay to keep servos unpowered until Arduino boots up
  X,Y,Z Limit Switches
  X,Y,Z Stepper Motors
  Eye Rig Servos
  24V DC Supplied via 24V DC Power Supply
  The Power to the 24V and 5V DC Power Supplies is supplied via the tilt switch/plug assembly mounted on the front of the electrical box. From this point 120V AC power is distributed to both power supplies.
  The sole purpose of the 24V DC Power Supply is to power the stepper motors via theTB6600 Stepper Motor Drivers.
  The 5V DC Power Supply was intended to power the cooling fan in addition to the Arduino itself via the barrel jack. However, it is currently only powering the cooling fan.
  The Arduino must be powered via a USB connection to a laptop or the surface on the rig itself. This is because every attempt to power it via the 5V PS resulted in very erratic servo movement. We initially believed that this was due to the barrel jack requiring between 7-12V instead of 5V. We then tried stepping down from the 24V PS with a buck converter set to vaules between 5-12V, however the erratic servo movement was still persistent.
  We now believe that it may be necessary to add capacitors in parallel to the power source for the Arduino. We ran out of time to investigate this issue any further, but have reason to believe that this may help smooth any voltage spikes/noise that may be introduced to the system.
  We suggest using this YouTube link to get some ideas. https://www.youtube.com/watch?v=oEMe6cXDNZs&ab_channel=electronzapdotcom
  USB Shield not shown. However, pin numbers are consistent.
